// Digital circuit main.dig as structural Verilog
module main (
  input  Clock,
  output [15:0] I,
  output [5:0] FUNCT
);

  wire AC, ALU_SRC, d_ff_5_q, d_ff_6_q, MEM_TO_REG, MR, Reg_dest, RW, Write_MEM;
  wire [1:0] AO;
  wire [4:0] d_ff_3_q, d_ff_4_q, multiplexer_1_out;
  wire [5:0] OPCODE;
  wire [23:0] ula_1_p5;
  wire [25:16] instruction_mem_1__32b__out;
  wire [31:0] _32x32_1_r_d1, _32x32_1_r_d2, add_1_s, bitextender_1_out, d_ff_1_q, d_ff_2_q, memory_24x32_1_d,
       multiplexer_2_out, pc_1_pc_out, R31, WB;
  wire [31:24] ula_1_p5_2;

  PC pc_1 (.Clok(Clock), .PC_IN(add_1_s), .PC_OUT(pc_1_pc_out));
  Add #(.Bits(32)) add_1 (.a(pc_1_pc_out), .b(32'h4), .c_i(1'b0), .s(add_1_s));  // open: c_o
  instruction_mem instruction_mem_1 (
    ._32b__ADDR(pc_1_pc_out), ._1b__Enable(Clock),
    ._32b__Out({OPCODE, instruction_mem_1__32b__out, I[15:6], FUNCT}));
  Control control_1 (
    .RgD(Reg_dest), .AluS(ALU_SRC), .MTR(MEM_TO_REG), .RW(RW), .MR(MR), .MW(Write_MEM), .AO_1(AO[0]),
    .AO_0(AO[1]), .Clk(Clock), .Op(OPCODE));  // open: B, J, APC
  D_FF #(.Bits(32)) d_ff_1 (.D(WB), .C(~Clock), .Q(d_ff_1_q));  // open: nQ
  D_FF #(.Bits(32)) d_ff_2 (.D(d_ff_1_q), .C(Clock), .Q(d_ff_2_q));  // open: nQ
  Multiplexer #(.Bits(5)) multiplexer_1 (
    .sel(Reg_dest), .in_0(instruction_mem_1__32b__out[20:16]), .in_1(I[15:11]), .out(multiplexer_1_out));
  D_FF #(.Bits(5)) d_ff_3 (.D(multiplexer_1_out), .C(~Clock), .Q(d_ff_3_q));  // open: nQ
  D_FF #(.Bits(5)) d_ff_4 (.D(d_ff_3_q), .C(Clock), .Q(d_ff_4_q));  // open: nQ
  _32x32 _32x32_1 (
    ._32_W_d(d_ff_2_q), ._5__R_reg1(instruction_mem_1__32b__out[25:21]),
    ._5__R_reg2(instruction_mem_1__32b__out[20:16]), ._5b__A_set(d_ff_4_q), .Clk(Clock), ._1__W_e(d_ff_6_q),
    .R_d1(_32x32_1_r_d1), .R_d2(_32x32_1_r_d2), .R31(R31));
  D_FF d_ff_5 (.D(RW), .C(~Clock), .Q(d_ff_5_q));  // open: nQ
  D_FF d_ff_6 (.D(d_ff_5_q), .C(Clock), .Q(d_ff_6_q));  // open: nQ
  BitExtender #(.inputBits(16), .outputBits(32)) bitextender_1 (.in({I[15:6], FUNCT}), .out(bitextender_1_out));
  Seven_Seg_Hex seven_seg_hex_1 (.d(R31[19:16]), .dp(1'b0));
  Seven_Seg_Hex seven_seg_hex_2 (.d(R31[15:12]), .dp(1'b0));
  Multiplexer #(.Bits(32)) multiplexer_2 (
    .sel(ALU_SRC), .in_0(_32x32_1_r_d2), .in_1(bitextender_1_out), .out(multiplexer_2_out));
  // ALU_Control alu_control_1: pin names not known; wires that end beside it: AO[0], AO[1], FUNCT, AC
  Seven_Seg_Hex seven_seg_hex_3 (.d(R31[11:8]), .dp(1'b0));
  Seven_Seg_Hex seven_seg_hex_4 (.d(R31[7:4]), .dp(1'b0));
  // ula ula_1: pin names not known; wires that end beside it: AC, _32x32_1_r_d1, multiplexer_2_out, {6{1'b0}}, {ula_1_p5_2, ula_1_p5}
  Seven_Seg_Hex seven_seg_hex_5 (.d(R31[3:0]), .dp(1'b0));
  memory_24x32 memory_24x32_1 (
    .A(ula_1_p5), .Data_in(_32x32_1_r_d2), .MW(Write_MEM), .Clk(Clock), .MR(MR), .D(memory_24x32_1_d));
  Multiplexer #(.Bits(32)) multiplexer_3 (
    .sel(MEM_TO_REG), .in_0({ula_1_p5_2, ula_1_p5}), .in_1(memory_24x32_1_d), .out(WB));

  assign I[5:0] = FUNCT;
endmodule
